# Fritzing sketch Leaf (saved by Fritzing 0.8.7b)

parts:
  U1 = NodeMCU V3.0
  ZS-042_RTC1 = ZS-042 RTC Module
  YF-S201_Flow_Meter1 = YF-S201 Water Flow Meter
  Part1 = FC-28 Soil Hygrometer Module
  Part2 = FC-28 Soil Hygrometer Module - Probe

nets:
  N1: U1.D1, ZS-042_RTC1.SCL
  N2: U1.D2, ZS-042_RTC1.SDA
  N3: U1.D7, YF-S201_Flow_Meter1.GND
  N4: U1.A0, Part1.AO
  VCC: ZS-042_RTC1.VCC, YF-S201_Flow_Meter1.VCC
  N5: Part1.POS, Part2.POS
  N6: Part1.NEG, Part2.NEG

custom parts:
  NodeMCU V3.0: ESP8266 based NodeMCU
  YF-S201 Water Flow Meter: The YF-S201 Flow Meter. The input voltage is 5V to 24V (DC).
  FC-28 Soil Hygrometer Module: The FC-28 is a soil hygrometer module that uses the Texas Instruments LM393 comparator chip to provide an analog measurement of soil humidity. The digital output is high when soil moisture is over a certain threshold, as determined by adjusting the potentiometer.
  FC-28 Soil Hygrometer Module - Probe: The FC-28 is a soil hygrometer module that uses the Texas Instruments LM393 comparator chip to provide an analog measurement of soil humidity.
